// Logisim project Nono-1.circ as structural Verilog: 11 circuits, main circuit main
module main (
  input  reset
);

  wire clock_1_out, Decodeur_d_instruction_isjmp, Decodeur_d_instruction_isload,
       Decodeur_d_instruction_regwrite;
  wire [1:0] Contole_de_saut_out_3;
  wire [2:0] Decodeur_d_instruction_ctrlual;
  wire [3:0] Selecteur_de_registre_rd, Selecteur_de_registre_rs, Selecteur_de_registre_rt_2, UAL_sf;
  wire [7:0] adder_1_out, adder_2_out, Banc_de_registre_rs_2, Banc_de_registre_rt_2, bit_extender_1_out,
       multiplexer_1_out, multiplexer_2_out, register_1_q, UAL_out_5;
  wire [15:0] ram_1_data;

  Clock clock_1 (.out(clock_1_out));
  Register register_1 (.D(multiplexer_2_out), .Q(register_1_q), .clk(clock_1_out), .clr(reset));  // open: en
  decodeur_instruction Decodeur_d_instruction (
    .opCode(ram_1_data[15:12]), .ctrlUAL(Decodeur_d_instruction_ctrlual),
    .isJMP(Decodeur_d_instruction_isjmp), .regWrite(Decodeur_d_instruction_regwrite),
    .isLoad(Decodeur_d_instruction_isload));
  Adder adder_1 (.a(register_1_q), .b(8'h1), .out(adder_1_out));  // open: cin, cout
  RAM #(.dataWidth(16)) ram_1 (.addr(register_1_q), .data(ram_1_data), .clk(clock_1_out));  // open: sel, ld, clr
  bancDeRegistre Banc_de_registre (
    .Reset(reset), .Clock(clock_1_out), .VallIn(multiplexer_1_out),
    .RegWrite(Decodeur_d_instruction_regwrite), .rd(Selecteur_de_registre_rt_2),
    .rs_2(Banc_de_registre_rs_2), .rs(Selecteur_de_registre_rd), .rt_2(Banc_de_registre_rt_2),
    .rt(Selecteur_de_registre_rs));
  selecteurDeRegistre Selecteur_de_registre (
    .rd_rs(ram_1_data[3:0]), .rs_rt(ram_1_data[7:4]), .rt(ram_1_data[11:8]),
    .isjmp(Decodeur_d_instruction_isjmp), .rd(Selecteur_de_registre_rd), .rs(Selecteur_de_registre_rs),
    .rt_2(Selecteur_de_registre_rt_2));
  Multiplexer #(.width(8)) multiplexer_1 (
    .in0(ram_1_data[7:0]), .in1(UAL_out_5), .out(multiplexer_1_out), .en(Decodeur_d_instruction_isload));  // open: sel
  assign bit_extender_1_out = {{4{ram_1_data[3]}}, ram_1_data[3:0]};  // Bit_Extender bit_extender_1
  Adder adder_2 (.a(adder_1_out), .b(bit_extender_1_out), .out(adder_2_out));  // open: cin, cout
  UAL UAL (
    .RS(Banc_de_registre_rs_2), .in_2(Banc_de_registre_rt_2), .Ctrl_UAL(Decodeur_d_instruction_ctrlual),
    .SF(UAL_sf), .out_5(UAL_out_5));
  controleDeSaut Contole_de_saut (.in_1(ram_1_data[15:12]), .of(UAL_sf), .out_3(Contole_de_saut_out_3));
  Multiplexer #(.select(2), .width(8)) multiplexer_2 (
    .in0(adder_1_out), .in1({8{1'b1}}), .in2(adder_2_out), .out(multiplexer_2_out),
    .sel(Contole_de_saut_out_3));  // open: in3, en

  // Notes on the sheet:
  //   Projet réalisé par Benjamin Dutriaux
  //   opcode
  //   isload
  //   isJMP
  //   regwrite
  //   ctrlUAL
  //   rd
  //   rs
  //   Valln
  //   rs
  //   rt
  //   opcode
  //   flag
  //   flag
endmodule

module UAL (
  input  [7:0] RS,
  input  [7:0] in_2,
  input  [2:0] Ctrl_UAL,
  output [3:0] SF,
  output [7:0] out_5
);

  wire [7:0] adder_1_out, AND_out, NOT_out, OR_out, shifter_1_out, shifter_2_out, subtractor_1_out;

  UAL_OF ual_of_1 (.in_1(RS), .in_2(in_2), .in_3(out_5), .OF(SF[0]));
  Adder adder_1 (.a(RS), .b(in_2), .out(adder_1_out), .cout(SF[1]));  // open: cin
  Subtractor subtractor_1 (.a(RS), .b(in_2), .out(subtractor_1_out), .bout(SF[2]));  // open: bin
  assign OR_out = RS | in_2;  // OR_Gate OR, 8 bits wide
  assign AND_out = RS & in_2;  // AND_Gate AND, 8 bits wide
  Shifter shifter_1 (.in(RS), .\dist (in_2[2:0]), .out(shifter_1_out));
  Shifter #(.shift("lr")) shifter_2 (.in(RS), .\dist (in_2[2:0]), .out(shifter_2_out));
  assign NOT_out = ~(RS | in_2);  // NOR_Gate NOT, 8 bits wide
  Multiplexer #(.select(3), .width(8)) multiplexer_1 (
    .in0(adder_1_out), .in1(subtractor_1_out), .in2(OR_out), .in3(AND_out), .in4(NOT_out),
    .in5(shifter_1_out), .in6(shifter_2_out), .out(out_5), .sel(Ctrl_UAL));  // open: in7, en
  Comparator comparator_1 (.b({8{1'b0}}), .eq(SF[3]));  // open: a, gt, lt

  // Notes on the sheet:
  //   RT
  //   OF
  //   Additioneur
  //   Soustracteur
  //   ZF
  //   OF
  //   Flag
  //   CF
  //   Sortie
endmodule

module UAL_OF (
  input  [7:0] in_1,
  input  [7:0] in_2,
  input  [7:0] in_3,
  output OF
);

  wire and_1_out, and_2_out, not_1_out, not_2_out, not_3_out;

  not not_1 (not_1_out, in_1[7]);
  not not_2 (not_2_out, in_2[7]);
  not not_3 (not_3_out, in_3[7]);
  and and_1 (and_1_out, in_1[7], in_2[7], not_3_out);
  and and_2 (and_2_out, not_1_out, not_2_out, in_3[7]);
  or or_1 (OF, and_2_out, and_1_out);
endmodule

module decodeur_instruction (
  input  [3:0] opCode,
  output [2:0] ctrlUAL,
  output isJMP,
  output regWrite,
  output isLoad
);

  ctrUAL_decodeur ctrual_decodeur_1 (.in_1(opCode), .out_2(ctrlUAL));
  isJmp_decodeur isjmp_decodeur_1 (.in_1(opCode), .out_2(isJMP));
  regWrite_decodeur regwrite_decodeur_1 (.in_1(opCode), .out_2(regWrite));
  isLoad_decodeur isload_decodeur_1 (.in_1(opCode), .out_2(isLoad));
endmodule

module regWrite_decodeur (
  input  [3:0] in_1,
  output out_2
);

  wire and_1_out, and_2_out, or_1_out;

  or or_1 (or_1_out, in_1[0], in_1[1], in_1[2]);
  and and_1 (and_1_out, ~in_1[0], ~in_1[0], ~in_1[0], ~in_1[0]);  // AND_Gate
  and and_2 (and_2_out, or_1_out, ~in_1[3]);  // AND_Gate
  or or_2 (out_2, and_2_out, and_1_out);
endmodule

module isLoad_decodeur (
  input  [3:0] in_1,
  output out_2
);

  and and_1 (out_2, in_1[0], in_1[1], in_1[2], ~in_1[3]);  // AND_Gate
endmodule

module isJmp_decodeur (
  input  [3:0] in_1,
  output out_2
);

  wire and_1_out, or_1_out, or_2_out;

  or or_1 (or_1_out, in_1[0], in_1[1], in_1[2]);
  and and_1 (and_1_out, or_1_out, in_1[3]);
  or or_2 (or_2_out, in_1[0], in_1[1], in_1[2], in_1[3]);
  and and_2 (out_2, or_2_out, and_1_out);
endmodule

module ctrUAL_decodeur (
  input  [3:0] in_1,
  output [2:0] out_2
);

  Multiplexer #(.width(3)) multiplexer_1 (
    .in0(in_1[2:0]), .in1({2'b00, in_1[3]}), .out(out_2), .sel(in_1[3]));  // open: en

  // Notes on the sheet:
  //   SI bit poids fort = 1, afficher 001
endmodule

module controleDeSaut (
  input  [3:0] in_1,
  input  [3:0] of,
  output [1:0] out_3
);

  wire and_2_out, and_3_out, and_4_out;

  and and_1 (out_3[0], ~in_1[0], ~in_1[1], ~in_1[2], in_1[3]);  // AND_Gate
  and and_2 (and_2_out, ~in_1[1], in_1[2], in_1[3]);  // AND_Gate
  and and_3 (and_3_out, in_1[0], ~in_1[1], in_1[3]);  // AND_Gate
  and and_4 (and_4_out, in_1[1], in_1[3]);
  or or_1 (out_3[1], and_2_out, and_3_out, and_4_out);

  // Notes on the sheet:
  //   0 = e3
  //   1 = e2
  //   2 = e1
  //   3 = e0
  //   sf
  //   cf
  //   zf
  //   Si 1000 sortie 01
  //   Si 0111 ou moins, sortie = 00
  //   Si 1001 ou plus sortie = 10
endmodule

module bancDeRegistre (
  input  Reset,
  input  Clock,
  input  [7:0] VallIn,
  input  [3:0] rs,
  input  [3:0] rt,
  input  RegWrite,
  input  [3:0] rd,
  output [7:0] rs_2,
  output [7:0] rt_2
);

  wire demultiplexer_2_out0, demultiplexer_2_out1, demultiplexer_2_out2, demultiplexer_2_out3,
       demultiplexer_2_out4, demultiplexer_2_out5, demultiplexer_2_out6, demultiplexer_2_out7,
       demultiplexer_2_out8, demultiplexer_2_out9, demultiplexer_2_out10, demultiplexer_2_out11,
       demultiplexer_2_out12, demultiplexer_2_out13, demultiplexer_2_out14, demultiplexer_2_out15;
  wire [7:0] _1, _2, _3, _4, _5, _6, _7, _8, _9, _10, _11, _12, _13, _14, _15, _16, register_1_q,
       register_2_q, register_3_q, register_4_q, register_5_q, register_6_q, register_7_q, register_8_q,
       register_9_q, register_10_q, register_11_q, register_12_q, register_13_q, register_14_q,
       register_15_q, register_16_q;

  Demultiplexer #(.select(4), .width(8)) demultiplexer_1 (
    .out0(_1), .out1(_2), .out2(_3), .out3(_4), .out4(_5), .out5(_6), .out6(_7), .out7(_8), .out8(_9),
    .out9(_10), .out10(_11), .out11(_12), .out12(_13), .out13(_14), .out14(_15), .out15(_16), .in(VallIn),
    .sel(rd));  // open: en
  Demultiplexer #(.select(4)) demultiplexer_2 (
    .out0(demultiplexer_2_out0), .out1(demultiplexer_2_out1), .out2(demultiplexer_2_out2),
    .out3(demultiplexer_2_out3), .out4(demultiplexer_2_out4), .out5(demultiplexer_2_out5),
    .out6(demultiplexer_2_out6), .out7(demultiplexer_2_out7), .out8(demultiplexer_2_out8),
    .out9(demultiplexer_2_out9), .out10(demultiplexer_2_out10), .out11(demultiplexer_2_out11),
    .out12(demultiplexer_2_out12), .out13(demultiplexer_2_out13), .out14(demultiplexer_2_out14),
    .out15(demultiplexer_2_out15), .in(RegWrite), .sel(rd));  // open: en
  Register register_1 (.D(_1), .en(demultiplexer_2_out0), .Q(register_1_q), .clk(Clock), .clr(Reset));
  Register register_2 (.D(_2), .en(demultiplexer_2_out1), .Q(register_2_q), .clk(Clock), .clr(Reset));
  Register register_3 (.D(_3), .en(demultiplexer_2_out2), .Q(register_3_q), .clk(Clock), .clr(Reset));
  Register register_4 (.D(_4), .en(demultiplexer_2_out3), .Q(register_4_q), .clk(Clock), .clr(Reset));
  Register register_5 (.D(_5), .en(demultiplexer_2_out4), .Q(register_5_q), .clk(Clock), .clr(Reset));
  Register register_6 (.D(_6), .en(demultiplexer_2_out5), .Q(register_6_q), .clk(Clock), .clr(Reset));
  Register register_7 (.D(_7), .en(demultiplexer_2_out6), .Q(register_7_q), .clk(Clock), .clr(Reset));
  Register register_8 (.D(_8), .en(demultiplexer_2_out7), .Q(register_8_q), .clk(Clock), .clr(Reset));
  Register register_9 (.D(_9), .en(demultiplexer_2_out8), .Q(register_9_q), .clk(Clock), .clr(Reset));
  Register register_10 (.D(_10), .en(demultiplexer_2_out9), .Q(register_10_q), .clk(Clock), .clr(Reset));
  Register register_11 (.D(_11), .en(demultiplexer_2_out10), .Q(register_11_q), .clk(Clock), .clr(Reset));
  Register register_12 (.D(_12), .en(demultiplexer_2_out11), .Q(register_12_q), .clk(Clock), .clr(Reset));
  Register register_13 (.D(_13), .en(demultiplexer_2_out12), .Q(register_13_q), .clk(Clock), .clr(Reset));
  Register register_14 (.D(_14), .en(demultiplexer_2_out13), .Q(register_14_q), .clk(Clock), .clr(Reset));
  Register register_15 (.D(_15), .en(demultiplexer_2_out14), .Q(register_15_q), .clk(Clock), .clr(Reset));
  Register register_16 (.D(_16), .en(demultiplexer_2_out15), .Q(register_16_q), .clk(Clock), .clr(Reset));
  Multiplexer #(.select(4), .width(8)) multiplexer_1 (
    .in0(register_1_q), .in1(register_2_q), .in2(register_3_q), .in3(register_4_q), .in4(register_5_q),
    .in5(register_6_q), .in6(register_7_q), .in7(register_8_q), .in8(register_9_q), .in9(register_10_q),
    .in10(register_11_q), .in11(register_12_q), .in12(register_13_q), .in13(register_14_q),
    .in14(register_15_q), .in15(register_16_q), .out(rs_2), .sel(rs));  // open: en
  Multiplexer #(.select(4), .width(8)) multiplexer_2 (
    .in0(register_1_q), .in1(register_2_q), .in2(register_3_q), .in3(register_4_q), .in4(register_5_q),
    .in5(register_6_q), .in6(register_7_q), .in7(register_8_q), .in8(register_9_q), .in9(register_10_q),
    .in10(register_11_q), .in11(register_12_q), .in12(register_13_q), .in13(register_14_q),
    .in14(register_15_q), .in15(register_16_q), .out(rt_2), .sel(rt));  // open: en

  // Other names for the same wires on the sheet: Clk = Clock; Rst = Reset
endmodule

module selecteurDeRegistre (
  input  [3:0] rd_rs,
  input  [3:0] rs_rt,
  input  [3:0] rt,
  input  isjmp,
  output [3:0] rd,
  output [3:0] rs,
  output [3:0] rt_2
);

  Multiplexer #(.width(4)) multiplexer_1 (.in0(rd_rs), .out(rd), .sel(isjmp));  // open: in1, en
  Multiplexer #(.width(4)) multiplexer_2 (.in0(rd_rs), .in1(rs_rt), .out(rs), .sel(isjmp));  // open: en
  Multiplexer #(.width(4)) multiplexer_3 (.in0(rs_rt), .in1(rt), .out(rt_2), .sel(isjmp));  // open: en
endmodule
